# Fritzing sketch Untitled Sketch 2 (saved by Fritzing 1.0.4)
breadboards: 1

parts:
  Arduino_Nano_Ble_33 = Arduino Nano (Rev3.0)
  Q1 = NPN-Transistor [package="TO92 [THT]"]
  R1 = Resistor [tolerance=±5% resistance=220 package="0805 [SMD]"]
  U1 = WS2812 RGB LED matrix 1x8
  U2 = Vibration Motor- ROB-08449 [package=vibe-motor-10mm]
  D1 = Schottky Diode [part_number=1N5817 package="300 mil [THT]"]

nets:
  GND: Arduino_Nano_Ble_33.GND, Q1.E, U1.GND
  N1: Arduino_Nano_Ble_33.D11/MOSI, U1.DIN
  N2: Arduino_Nano_Ble_33.D12/MISO, R1.Pin_1
  5V: Arduino_Nano_Ble_33.5V, U1.VCC, U2.-, D1.cathode
  N3: Q1.B, U2.+, D1.anode
  N4: Q1.C, R1.Pin_0

custom parts:
  WS2812 RGB LED matrix 1x8: WS2812 matrix 1x8
